# Fritzing sketch 433Mhz_WeMos_Circuit (saved by Fritzing 0.9.3b)
breadboards: 2

parts:
  U6 = RF-LINK_TX [package=rf-link_tx]
  U7 = RF-LINK_RX [package=rf-link_rx]
  WeMos_D1_Mini1 = WeMos D1 Mini
  WeMos_D1_Mini2 = WeMos D1 Mini

nets:
  N1: U6.DATA, WeMos_D1_Mini1.D7
  N2: U6.GND, WeMos_D1_Mini1.G
  +5V: U6.+5V, WeMos_D1_Mini1.5V
  N3: U7.GND, WeMos_D1_Mini2.G
  N4: U7.Data#2, WeMos_D1_Mini2.D7
  VCC: U7.VCC, WeMos_D1_Mini2.5V

notes:
  433Mhz Receiver Circuit
  433Mhz Transmitter Circuit

custom parts:
  RF-LINK_TX: Common RF transmitter of the 315.00Mhz varity
  RF-LINK_RX: RF Link receivers- WRL-8947, 8948, 8949, 8950
